// Digital circuit Template-01.dig as structural Verilog
module Template_01 (
  input  [3:0] In,
  output A,
  output B,
  output C,
  output D,
  output E,
  output F,
  output G
);

  wire _2_3, _2_4, _2_4_t, _3_4, _23, _23_4, _234, _234_t, not_1_out, not_2_out, not_3_out, not_4_out,
       not_5_out, not_6_out, not_7_out, not_8_out, not_9_out, or_1_out, or_2_out;

  not not_1 (not_1_out, In[2]);
  not not_2 (not_2_out, In[1]);
  not not_3 (not_3_out, In[2]);
  not not_4 (not_4_out, In[0]);
  not not_5 (not_5_out, In[0]);
  not not_6 (not_6_out, In[1]);
  not not_7 (not_7_out, In[0]);
  not not_8 (not_8_out, In[2]);
  not not_9 (not_9_out, In[1]);
  and and_1 (_234, In[2], In[1], In[0]);
  and and_2 (_2_3, not_1_out, In[1]);
  and and_3 (_23_4, In[2], not_2_out, In[0]);
  and and_4 (_2_4_t, not_3_out, not_4_out);
  and and_5 (_234_t, In[2], In[1], not_5_out);
  and and_6 (_3_4, not_6_out, not_7_out);
  and and_7 (_2_4, not_8_out, In[0]);
  and and_8 (_23, In[2], not_9_out);
  or or_1 (or_1_out, _234, _2_3, _23_4);
  or or_2 (or_2_out, _2_4_t, _234_t, In[3]);
  or or_3 (B, _2_4, _3_4, _234, _2_4_t);
  or or_4 (C, _2_4, _3_4, _234, _23_4, _234_t);
  or or_5 (D, _2_3, _23_4, _2_4_t, _234_t, In[3]);
  or or_6 (E, _2_4_t, _234_t);
  or or_7 (F, _3_4, _234, _23_4, _234_t, In[3]);
  or or_8 (G, _23, _2_3, _234_t, In[3]);
  or or_9 (A, or_1_out, or_2_out);
  Seven_Seg seven_seg_1 (.a(A), .b(B), .c(C), .d(D), .e(E), .f(F), .g(G), .dp(1'b0));

  // Other names for the same wires on the sheet: I4 = In[0]; I3 = In[1]; I2 = In[2]; I1 = In[3]
endmodule
