// Digital circuit Template-02.dig as structural Verilog
module Template_02 (
  input  [2:0] In,
  input  clk,
  output [7:0] Z,
  output A,
  output B,
  output C,
  output D,
  output E,
  output F,
  output G,
  output H
);

  wire _1_2_3, _1_23, _1_23_t, _2_3, _12, _12_3, _12_3_t, _23, _123, not_1_out, not_2_out, not_3_out,
       not_4_out, not_5_out, not_6_out, not_7_out, not_8_out, not_9_out, not_10_out, not_11_out, not_12_out,
       or_1_out, or_2_out;

  not not_1 (not_1_out, In[2]);
  not not_2 (not_2_out, In[1]);
  not not_3 (not_3_out, In[0]);
  not not_4 (not_4_out, In[2]);
  not not_5 (not_5_out, In[1]);
  not not_6 (not_6_out, In[1]);
  not not_7 (not_7_out, In[0]);
  not not_8 (not_8_out, In[1]);
  not not_9 (not_9_out, In[0]);
  not not_10 (not_10_out, In[2]);
  not not_11 (not_11_out, In[0]);
  not not_12 (not_12_out, In[1]);
  and and_1 (_1_23, not_1_out, In[1], In[0]);
  and and_2 (_123, In[2], In[1], In[0]);
  and and_3 (_2_3, not_2_out, not_3_out);
  and and_4 (_1_2_3, not_4_out, not_5_out, In[0]);
  and and_5 (_12, In[2], not_6_out);
  and and_6 (_23, In[1], not_7_out);
  and and_7 (_12_3_t, In[2], not_8_out, not_9_out);
  and and_8 (_1_23_t, not_10_out, In[1], not_11_out);
  and and_9 (_12_3, In[2], not_12_out, In[0]);
  or or_1 (or_1_out, _1_23, _123, _2_3);
  or or_2 (or_2_out, _1_2_3, _12, _23);
  or or_3 (C, _12_3_t, _123, _1_2_3, _23);
  or or_4 (E, _1_23, _1_2_3, _12);
  or or_5 (F, _1_23_t, _1_23, _2_3, _12);
  or or_6 (G, _1_23_t, _12_3_t, _123);
  or or_7 (H, _12_3_t, _1_2_3, _23);
  or or_8 (B, or_1_out, or_2_out);
  Terminal terminal_1 (.D({1'b0, B, C, 1'b0, E, F, G, H}), .C(clk), .en(1'b1));

  assign A = 1'b0;
  assign D = 1'b0;
  assign Z = {1'b0, B, C, 1'b0, E, F, G, H};

  // Other names for the same wires on the sheet: I3 = In[0]; I2 = In[1]; I1 = In[2]

  // Notes on the sheet:
  //   clk: Hz: 100
endmodule
