// Digital circuit Template-03.dig as structural Verilog
module Template_03 (
  input  [3:0] In,
  input  [1:0] Selector,
  output [3:0] Output
);

  wire _1_2, _1_2_3, _1_3_4, _1_4, _1_4_t, _1_23, _1_23_4, _1_23_4_t, _1_23_t, _1_24, _1_24_t, _1_34,
       _1_34_t, _2_3_4, _2_3_4_t, _12_3, _21, _22, _23, _24, _61, _62, _63, _64, C2, C3, C4, E1, E2, E3, E4,
       not_1_out, not_2_out, not_3_out, not_4_out, not_5_out, not_6_out, not_7_out, not_8_out, not_9_out,
       not_10_out, not_11_out, not_12_out, not_13_out, not_14_out, not_15_out, not_16_out, not_17_out,
       not_18_out, not_19_out, not_20_out, not_21_out, not_22_out, not_23_out, not_24_out, not_25_out,
       not_26_out, not_27_out, not_28_out, not_29_out;

  and and_1 (_1_23, not_1_out, In[2], In[1]);
  not not_1 (not_1_out, In[3]);
  and and_2 (_12_3, In[3], not_2_out, not_3_out);
  not not_2 (not_2_out, In[2]);
  not not_3 (not_3_out, In[1]);
  and and_3 (_1_24, not_4_out, In[2], In[0]);
  not not_4 (not_4_out, In[3]);
  and and_4 (_2_3_4, not_5_out, not_6_out, In[0]);
  not not_5 (not_5_out, In[2]);
  not not_6 (not_6_out, In[1]);
  and and_5 (_1_23_4_t, not_7_out, In[2], not_8_out, not_9_out);
  not not_7 (not_7_out, In[3]);
  not not_8 (not_8_out, In[1]);
  not not_9 (not_9_out, In[0]);
  and and_6 (_1_34, not_10_out, In[1], In[0]);
  not not_10 (not_10_out, In[3]);
  and and_7 (_2_3_4_t, not_11_out, not_12_out, not_13_out);
  not not_11 (not_11_out, In[2]);
  not not_12 (not_12_out, In[1]);
  not not_13 (not_13_out, In[0]);
  and and_8 (_1_4_t, not_14_out, not_15_out);
  not not_14 (not_14_out, In[3]);
  not not_15 (not_15_out, In[0]);
  and and_9 (_1_2, not_16_out, In[2]);
  not not_16 (not_16_out, In[3]);
  and and_10 (_1_3_4, not_17_out, not_18_out, In[0]);
  not not_17 (not_17_out, In[3]);
  not not_18 (not_18_out, In[1]);
  and and_11 (_1_34_t, not_19_out, In[1], not_20_out);
  not not_19 (not_19_out, In[3]);
  not not_20 (not_20_out, In[0]);
  and and_12 (_1_23_4, not_21_out, In[2], not_22_out, In[0]);
  not not_21 (not_21_out, In[3]);
  not not_22 (not_22_out, In[1]);
  and and_13 (_1_24_t, not_23_out, In[2], not_24_out);
  not not_23 (not_23_out, In[3]);
  not not_24 (not_24_out, In[0]);
  and and_14 (_1_4, not_25_out, In[0]);
  not not_25 (not_25_out, In[3]);
  and and_15 (_1_23_t, not_26_out, In[2], not_27_out);
  not not_26 (not_26_out, In[3]);
  not not_27 (not_27_out, In[1]);
  and and_16 (_1_2_3, not_28_out, not_29_out, In[1]);
  not not_28 (not_28_out, In[3]);
  not not_29 (not_29_out, In[2]);
  or or_1 (E1, _1_23, _12_3, _1_24);
  or or_2 (E2, _2_3_4, _1_23_4_t, _1_2_3);
  or or_3 (E3, _1_23_4_t, _1_34, _2_3_4_t);
  or or_4 (E4, _2_3_4_t, _1_4_t);
  or or_5 (C2, _12_3, _1_2);
  or or_6 (C3, _1_2_3, _1_23_t);
  or or_7 (C4, _1_3_4, _1_34_t, _2_3_4);
  or or_8 (_21, _1_23_4, _1_23, _12_3);
  or or_9 (_22, _1_24_t, _1_23, _12_3);
  or or_10 (_23, _1_2_3, _1_23_4, _12_3);
  or or_11 (_24, _2_3_4, _1_4);
  or or_12 (_61, _12_3, _1_23_4, _1_34);
  or or_13 (_62, _1_23, _1_24_t, _2_3_4);
  or or_14 (_63, _12_3, _1_34_t, _1_23_4);
  or or_15 (_64, _2_3_4, _1_23_4, _1_34);
  Multiplexer #(.Bits(4), .Selector_Bits(2)) multiplexer_1 (
    .sel(Selector), .in_0({E1, E2, E3, E4}), .in_1({_12_3, C2, C3, C4}), .in_2({_21, _22, _23, _24}),
    .in_3({_61, _62, _63, _64}), .out(Output));

  // Other names for the same wires on the sheet: I4 = In[0]; I3 = In[1]; I2 = In[2]; I1 = In[3]; _0 = Selector[0];
  //   _1 = Selector[1]
endmodule
