// Digital circuit Template-04.dig as structural Verilog
module Template_04 (
  input  [6:0] In,
  output [6:0] Output
);

  wire C1, C2, C3;
  wire [6:3] H;

  xor xor_1 (C1, In[3], In[4], In[5], In[6]);
  xor xor_2 (C2, In[1], In[2], In[5], In[6]);
  xor xor_3 (C3, In[0], In[2], In[4], In[6]);
  Demultiplexer demultiplexer_1 (.in(1'b1));  // open: sel, out_0, out_1
  xor xor_4 (Output[0], In[6], H[6]);
  // Pins of 1 and 7 bits meet at Output
  // Pins of 3 and 7 bits meet at {H, C3, C2, C1}
  // Pins of 1 and 7 bits meet at {In[0], In[1], In[2], In[3], In[4], In[5], In[6]}
  // Pins of 1 and 7 bits meet at {C1, C2, C3, H[3], H[4], H[5], H[6]}

  // Other names for the same wires on the sheet: H[2:0] = {C3, C2, C1}; S1 = C1; S2 = C2; S3 = C3; S4 = H[3];
  //   S5 = H[4]; S6 = H[5]; S7 = H[6]; _1 = In[0]; _2 = In[1]; _3 = In[2]; _4 = In[3]; _5 = In[4]; _6 = In[5];
  //   _7 = In[6]
endmodule
