// Digital circuit Template.dig as structural Verilog
module Template (
  input  Cin,
  input  B,
  input  A,
  output Sum,
  output Cout
);

  wire and_1_out, and_2_out, and_3_out, and_4_out, and_5_out, and_6_out, and_7_out, and_8_out, not_1_out,
       not_2_out, not_3_out;

  or or_1 (Cout, and_4_out, and_3_out, and_2_out, and_1_out);
  and and_1 (and_1_out, Cin, B, not_1_out);
  and and_2 (and_2_out, Cin, not_2_out, A);
  and and_3 (and_3_out, not_3_out, B, A);
  and and_4 (and_4_out, Cin, B, A);
  not not_1 (not_1_out, A);
  not not_2 (not_2_out, B);
  not not_3 (not_3_out, Cin);
  and and_5 (and_5_out, not_1_out, not_2_out, Cin);
  and and_6 (and_6_out, not_1_out, B, not_3_out);
  and and_7 (and_7_out, A, not_2_out, not_3_out);
  and and_8 (and_8_out, A, B, Cin);
  or or_2 (Sum, and_5_out, and_6_out, and_7_out, and_8_out);
endmodule
