// Digital circuit Template.dig as structural Verilog
module Template (
  input  A,
  input  B,
  input  Cin,
  output Sum,
  output Cout
);

  wire and_1_out, and_2_out, and_3_out, and_4_out, not_1_out, not_2_out, not_3_out, or_2_out, or_3_out,
       or_4_out, or_5_out;

  or or_1 (Cout, and_4_out, and_3_out, and_2_out, and_1_out);
  and and_1 (and_1_out, Cin, B, not_1_out);
  and and_2 (and_2_out, Cin, not_2_out, A);
  and and_3 (and_3_out, not_3_out, B, A);
  and and_4 (and_4_out, Cin, B, A);
  not not_1 (not_1_out, A);
  not not_2 (not_2_out, B);
  not not_3 (not_3_out, Cin);
  or or_2 (or_2_out, not_1_out, not_2_out, Cin);
  or or_3 (or_3_out, not_1_out, B, not_3_out);
  or or_4 (or_4_out, A, not_2_out, not_3_out);
  or or_5 (or_5_out, A, B, Cin);
  and and_5 (Sum, or_2_out, or_3_out, or_4_out, or_5_out);
endmodule
