// Digital circuit Template.dig as structural Verilog
module Template (
  input  A,
  input  B,
  input  C,
  input  D,
  output Z1,
  output Z2,
  output Z3
);

  wire not_1_out, not_2_out, not_3_out, not_4_out, not_5_out, not_6_out, not_7_out, not_8_out, not_9_out,
       not_10_out, not_11_out, not_12_out, not_13_out, not_14_out, not_15_out, not_16_out, not_17_out,
       not_18_out, not_19_out, not_20_out, not_21_out, not_22_out, not_23_out, not_24_out, not_25_out,
       not_26_out, not_27_out, not_28_out, not_29_out, not_30_out, not_31_out, not_32_out, not_33_out,
       not_34_out, not_35_out, not_36_out, not_37_out, not_38_out, not_39_out, not_40_out, not_41_out,
       not_42_out, not_43_out, not_44_out, not_45_out, not_46_out, not_47_out, not_48_out, not_49_out,
       not_50_out, not_51_out, not_52_out, not_53_out, not_54_out, not_55_out, not_56_out, not_57_out,
       not_58_out, not_59_out, not_60_out, not_61_out, not_62_out, not_63_out, not_64_out, or_1_out,
       or_2_out, or_3_out, or_4_out, or_5_out, or_6_out, or_7_out, or_8_out, or_9_out, or_10_out, or_11_out,
       or_12_out, or_13_out, or_14_out, or_15_out, or_16_out, or_17_out, or_18_out, or_19_out, or_20_out,
       or_21_out, or_22_out, or_23_out, or_24_out, or_25_out, or_26_out, or_27_out, or_28_out, or_29_out,
       or_30_out, or_31_out, or_32_out;

  or or_1 (or_1_out, A, B, C, D);
  or or_2 (or_2_out, A, B, C, not_1_out);
  not not_1 (not_1_out, D);
  or or_3 (or_3_out, A, B, not_2_out, D);
  not not_2 (not_2_out, C);
  or or_4 (or_4_out, A, B, not_3_out, not_4_out);
  not not_3 (not_3_out, C);
  not not_4 (not_4_out, D);
  or or_5 (or_5_out, A, not_5_out, C, not_6_out);
  not not_5 (not_5_out, B);
  not not_6 (not_6_out, D);
  or or_6 (or_6_out, A, not_7_out, not_8_out, D);
  not not_7 (not_7_out, B);
  not not_8 (not_8_out, C);
  or or_7 (or_7_out, A, not_9_out, not_10_out, not_11_out);
  not not_9 (not_9_out, B);
  not not_10 (not_10_out, C);
  not not_11 (not_11_out, D);
  not not_12 (not_12_out, A);
  or or_8 (or_8_out, not_12_out, B, not_13_out, D);
  not not_13 (not_13_out, C);
  not not_14 (not_14_out, A);
  or or_9 (or_9_out, not_14_out, B, not_15_out, not_16_out);
  not not_15 (not_15_out, C);
  not not_16 (not_16_out, D);
  not not_17 (not_17_out, A);
  or or_10 (or_10_out, not_17_out, not_18_out, not_19_out, not_20_out);
  not not_18 (not_18_out, B);
  not not_19 (not_19_out, C);
  not not_20 (not_20_out, D);
  or or_11 (or_11_out, A, B, C, D);
  or or_12 (or_12_out, A, not_21_out, C, D);
  not not_21 (not_21_out, B);
  or or_13 (or_13_out, A, not_22_out, C, not_23_out);
  not not_22 (not_22_out, B);
  not not_23 (not_23_out, D);
  or or_14 (or_14_out, not_24_out, B, C, D);
  not not_24 (not_24_out, A);
  or or_15 (or_15_out, not_25_out, B, C, not_26_out);
  not not_25 (not_25_out, A);
  not not_26 (not_26_out, D);
  or or_16 (or_16_out, not_27_out, B, not_28_out, D);
  not not_27 (not_27_out, A);
  not not_28 (not_28_out, C);
  or or_17 (or_17_out, not_29_out, not_30_out, C, D);
  not not_29 (not_29_out, A);
  not not_30 (not_30_out, B);
  or or_18 (or_18_out, not_31_out, not_32_out, C, not_33_out);
  not not_31 (not_31_out, A);
  not not_32 (not_32_out, B);
  not not_33 (not_33_out, D);
  or or_19 (or_19_out, not_34_out, not_35_out, not_36_out, D);
  not not_34 (not_34_out, A);
  not not_35 (not_35_out, B);
  not not_36 (not_36_out, C);
  or or_20 (or_20_out, not_37_out, not_38_out, not_39_out, not_40_out);
  not not_37 (not_37_out, A);
  not not_38 (not_38_out, B);
  not not_39 (not_39_out, C);
  not not_40 (not_40_out, D);
  not not_41 (not_41_out, D);
  not not_42 (not_42_out, C);
  not not_43 (not_43_out, C);
  not not_44 (not_44_out, D);
  not not_45 (not_45_out, B);
  not not_46 (not_46_out, B);
  not not_47 (not_47_out, C);
  not not_48 (not_48_out, B);
  not not_49 (not_49_out, C);
  not not_50 (not_50_out, D);
  not not_51 (not_51_out, A);
  not not_52 (not_52_out, A);
  not not_53 (not_53_out, D);
  not not_54 (not_54_out, A);
  not not_55 (not_55_out, C);
  not not_56 (not_56_out, D);
  not not_57 (not_57_out, A);
  not not_58 (not_58_out, B);
  not not_59 (not_59_out, A);
  not not_60 (not_60_out, B);
  not not_61 (not_61_out, D);
  not not_62 (not_62_out, A);
  not not_63 (not_63_out, B);
  not not_64 (not_64_out, C);
  or or_21 (or_21_out, A, B, C, not_41_out);
  or or_22 (or_22_out, A, B, not_42_out, D);
  or or_23 (or_23_out, A, B, not_43_out, not_44_out);
  or or_24 (or_24_out, A, not_45_out, C, D);
  or or_25 (or_25_out, A, not_46_out, not_47_out, D);
  or or_26 (or_26_out, A, not_48_out, not_49_out, not_50_out);
  or or_27 (or_27_out, not_51_out, B, C, D);
  or or_28 (or_28_out, not_52_out, B, C, not_53_out);
  or or_29 (or_29_out, not_54_out, B, not_55_out, not_56_out);
  or or_30 (or_30_out, not_57_out, not_58_out, C, D);
  or or_31 (or_31_out, not_59_out, not_60_out, C, not_61_out);
  or or_32 (or_32_out, not_62_out, not_63_out, not_64_out, D);
  and and_1 (Z1, or_1_out, or_2_out, or_3_out, or_4_out, or_5_out, or_6_out, or_7_out, or_8_out, or_9_out, or_10_out);
  and and_2 (Z2, or_11_out, or_12_out, or_13_out, or_14_out, or_15_out, or_16_out, or_17_out, or_18_out, or_19_out, or_20_out);
  and and_3 (Z3, or_21_out, or_22_out, or_23_out, or_24_out, or_25_out, or_26_out, or_27_out, or_28_out, or_29_out, or_30_out, or_31_out, or_32_out);
endmodule
