// Digital circuit Template.dig as structural Verilog
module Template (
  input  X0,
  input  X1,
  input  Selector,
  output Z
);

  wire and_1_out, and_2_out, S_t;

  not not_1 (S_t, Selector);
  and and_1 (and_1_out, X0, S_t);
  and and_2 (and_2_out, Selector, X1);
  or or_1 (Z, and_1_out, and_2_out);

  // Other names for the same wires on the sheet: S = Selector
endmodule
