// Digital circuit Template.dig as structural Verilog
module Template (
  input  X0,
  input  X1,
  input  Selector,
  output Z
);

  wire or_1_out, or_2_out, S_t;

  not not_1 (S_t, Selector);
  or or_1 (or_1_out, X0, Selector);
  or or_2 (or_2_out, S_t, X1);
  and and_1 (Z, or_1_out, or_2_out);

  // Other names for the same wires on the sheet: S = Selector
endmodule
